// Logisim project CtrlMode.circ as structural Verilog: 1 circuit, main circuit main
module main (
  input  ena,
  input  [3:0] cmd_7_4,
  input  [3:0] cmd_3_0,
  output caught,
  output get,
  output show,
  output [3:0] address_no
);

  wire and_1_out, and_2_out, decoder_1_out0, decoder_1_out2, decoder_1_out3, decoder_2_out0, decoder_2_out1,
       decoder_2_out2, decoder_2_out3, not_1_out;
  wire [3:0] adder_1_out, controlled_buffer_1_out, controlled_buffer_2_out;

  Decoder #(.select(4)) decoder_1 (
    .out0(decoder_1_out0), .out2(decoder_1_out2), .out3(decoder_1_out3), .sel(cmd_7_4), .en(1'b1));  // open: out1, out4, out5, out6, out7, out8, out9, out10, out11, out12, out13, out14, out15
  Decoder #(.select(4)) decoder_2 (
    .out0(decoder_2_out0), .out1(decoder_2_out1), .out2(decoder_2_out2), .out3(decoder_2_out3),
    .sel(cmd_3_0), .en(1'b1));  // open: out4, out5, out6, out7, out8, out9, out10, out11, out12, out13, out14, out15
  assign controlled_buffer_1_out = decoder_1_out0 ? cmd_3_0 : 4'bz;  // Controlled_Buffer controlled_buffer_1
  and and_1 (and_1_out, decoder_1_out3, decoder_1_out0);
  and and_2 (and_2_out, ena, decoder_1_out2);
  Register #(.width(4)) register_1 (
    .D(controlled_buffer_1_out), .en(and_1_out), .Q(address_no), .clk(ena));  // open: clr
  assign controlled_buffer_2_out = decoder_2_out0 ? 4'b1111 : 4'bz;  // Controlled_Buffer controlled_buffer_2
  assign controlled_buffer_2_out = decoder_2_out1 ? 4'b0001 : 4'bz;  // Controlled_Buffer controlled_buffer_3
  D_Flip_Flop d_ff_1 (.clk(and_2_out), .D(decoder_2_out1), .Q(caught), .en(1'b1));  // open: Qn, preset, reset
  D_Flip_Flop d_ff_2 (.clk(and_2_out), .D(decoder_2_out2), .Q(get), .en(1'b1));  // open: Qn, preset, reset
  D_Flip_Flop d_ff_3 (.clk(and_2_out), .D(decoder_2_out3), .Q(show), .en(1'b1));  // open: Qn, preset, reset
  Adder #(.width(4)) adder_1 (.a(address_no), .b(controlled_buffer_2_out), .out(adder_1_out));  // open: cin, cout
  not not_1 (not_1_out, decoder_1_out0);
  assign controlled_buffer_1_out = not_1_out ? adder_1_out : 4'bz;  // Controlled_Buffer controlled_buffer_4
endmodule
